# Fritzing sketch 2Leds (saved by Fritzing 0.9.1b)
breadboards: 1

parts:
  Composant2 = Arduino Wireless SD Shield
  R1 = Resistor [tolerance=±5% resistance=220 package=THT]
  LED1 = LED - 5mm [color="Red (633nm)" package="5 mm [THT]"]
  LED2 = LED - 5mm [color="Red (633nm)" package="5 mm [THT]"]
  R2 = Resistor [tolerance=±5% resistance=220 package=THT]

nets:
  N1: Composant2.D12, R2.Pin_1
  N2: Composant2.D13, R1.Pin_1
  N3: Composant2.GND, LED1.cathode, LED2.cathode
  N4: R1.Pin_0, LED1.anode
  N5: LED2.anode, R2.Pin_0
