# Fritzing sketch exampleswitch (saved by Fritzing 0.9.1b)
breadboards: 1

parts:
  Composant2 = Arduino Wireless SD Shield
  S1 = Pushbutton [package="[THT]"]
  S2 = Toggle Switch [package=THT]
  S3 = Toggle Switch [package=THT]
  R3 = Resistor [tolerance=±5% resistance=220 package=THT]
  R4 = Resistor [tolerance=±5% resistance=220 package=THT]
  R5 = Resistor [tolerance=±5% resistance=220 package=THT]

nets (from the breadboard view):
  N1: Composant2.D9, S1.Pin_1, S1.Pin_2, R5.Pin_0
  N2: Composant2.D10, S2.COM
  N3: Composant2.D11, S3.COM
  N4: Composant2.3.3V, S1.Pin_3, S1.Pin_4, R3.Pin_0, R4.Pin_0
  N5: Composant2.GND, S2.L2, S3.L2, R5.Pin_1
  N6: S2.L1, R4.Pin_1
  N7: S3.L1, R3.Pin_1
